# Fritzing sketch TemperaturSensor (saved by Fritzing 0.9.3b)
circuit board: 8.46667cm x 5.64444cm
breadboards: 1

parts:
  J1 = male pin header, 4 pins [form="♂ (male)"]
  DS1 = DS18B20 1-Wire Temperature Sensor [part_number=DS18B20]
  R1 = Resistor [tolerance=±5% resistance=4.7k package=THT]
  LED1 = LED - 5mm [color="Red (633nm)" package="5 mm [THT]"]
  R2 = Resistor [tolerance=±5% resistance=220 package=THT]

nets:
  N1: J1.pin1, DS1.GND, R2.Pin_0
  N2: J1.pin2, DS1.DQ, R1.Pin_0
  N3: J1.pin3, DS1.VDD, R1.Pin_1
  N4: J1.pin4, LED1.anode
  N5: LED1.cathode, R2.Pin_1

notes:
  Pin1: Ground (6)
  Pin2: Sensor (7)
  Pin3: 3V3 (1)
  Pin4: GPIO (11)
